// Logisim project control_logic.circ as structural Verilog: 1 circuit, main circuit control_logic
module control_logic (
  input  [31:0] inst,
  input  BrEq,
  input  BrLt,
  output PCSel,
  output RegWEn,
  output [2:0] ImmSel,
  output BrUn,
  output ASel,
  output BSel,
  output [3:0] ALUSel,
  output MemRW,
  output [1:0] WBSel
);

  wire [2:0] adder_1_out, adder_2_out, multiplexer_1_out, multiplexer_2_out;

  Multiplexer #(.width(3), .enable("false")) multiplexer_1 (
    .in0(inst[6:4]), .in1(adder_1_out), .out(multiplexer_1_out), .sel(inst[2]));
  Adder #(.width(3)) adder_1 (.a(inst[6:4]), .b(3'b001), .out(adder_1_out));  // open: cin, cout
  Multiplexer #(.width(3), .enable("false")) multiplexer_2 (
    .in0(inst[6:4]), .in1(adder_2_out), .out(multiplexer_2_out), .sel(inst[3]));
  Adder #(.width(3)) adder_2 (.a(inst[6:4]), .b(3'b111), .out(adder_2_out));  // open: cin, cout
  Multiplexer #(.width(3), .enable("false")) multiplexer_3 (
    .in0(multiplexer_1_out), .in1(multiplexer_2_out), .out(ImmSel), .sel(inst[3]));
  // Probe on ImmSel

  // Other names for the same wires on the sheet: op[6:0] = inst[6:0]; rd[4:0] = inst[11:7]; func3[2:0] = inst[14:12];
  //   r1[4:0] = inst[19:15]; r2[4:0] = inst[24:20]; func7[6:0] = inst[31:25]

  // Notes on the sheet:
  //   INPUTS to your circuit
  //   DON'T CHANGE THE LOCATIONS OF THE INPUTS AND OUTPUTS!
  //   OUTPUT from your circuit
endmodule
